// Logisim project arithmetic_logic.circ as structural Verilog: 11 circuits, main circuit main
module main (
  input  [8:0] Sign,
  input  [8:0] Sign_2,
  output [7:0] out_3,
  output out_4,
  output out_5
);

  wire and_1_out, and_2_out, and_3_out, and_4_out, and_5_out, and_6_out, and_7_out, button_1_out,
       control_unit_1_negate, not_1_out, not_2_out, not_3_out, or_1_out, or_2_out, overflowdetection_1_v,
       synchroniser_1_clk, synchroniser_1_done;
  wire [1:0] synchroniser_1_counter;
  wire [7:0] control_unit_1_outa, control_unit_1_outb, register_8bit_1_q;

  // Image #(.height(298), .image("data:image/png;base64,iVBORw0KGgoAAAANSUhEUgAAAGsAAAEqCAYAAAASzK5xAAAMY0lEQVR4Xu2dz4slVxXHa4hgdCFxkcGRLALqQhQUVMzCjSABN+7GTaDb9K1+01kEnJW4anCeImKyy2LwP5AsXRmymR5HScZW0pCRCGFAHCL+QEHJL52xzqu6/eqduj+r7rnv3dT3A5fuV+fcc5vv99337rv1qquqAAAAAAAAAAAAAEJZVtUJNX4c7CCNUQ+o8eNgB4FZBQGzCgJmFQTMKgiYVRAwqyBgVkHArIKAWQUBswoCZhUEzCoImLVFrlXVjxrx39cmCLX3aRw+NoikEfJdg7gS7V0+NojEIKpY42ODSKTFlK4/K6TFlK4/K6TFlK4/K6TFlK6fH6VOqrp+YGxK3Wl+7lWXLz/Eu6VAWkzp+vnhBpmaUjd4txRIiyldPz/aEA7NJppVOn50dJGnTEVaTOn6+bGZpanrm13OTR6airSY0vXz4zOLZpQvZyTSYkrXz4/PiPbl0J0zEmkxpevnx2fE+n3rdR6airSY0vXzYzNLLzCUutfl7PGUqUiLKV0/P9osV1PqVxKftaTFlK6fH27Mpkn4ULxTaGM0Bwefbx6/vTp2ePitXmZypMWUrp8fbhah1NVuZv21WiwubcQSIi2mdP38mMyqqgvNsV90sV+uHgsgLaZ0/fyYzdIfht/q4t/l4RRIiyldPz82s4jDw282sfvNy+E7zc8v8vBUpMWUrp8fl1mEUi90Ob/noalIiyldPz90PouajatXP9LEf+PMGYm0mNL1Z4W0mNL1Z4W0mNL1Z4W0mNL1Z4W0mNL1Z4W0mNL1Z4W0mNL1Z4W0mNL1Z4W0mNL1Z4W0mNL1Z4W0mNL1Z4W0mNL1Z4W0mNL1Z4W0mNL13Vd10FeYTd85d/fZbL7d8/ak421vXgKkxZSu7/62kU3wGLPq+nSjb5/WqLPzXGGkxZSubz8Z2AqpLxIYxl0o9VzX72/N75/m4RXtlzpPN4wVRlpM6fp2szS+OKeuv7PKV+q96uDg6zx8jv6atFJvRo8xEmkxpev7zfDF+ywWX+u+P0F9Fjy8YvgSur4mSxhpMaXr+83wxTVXrjzeGPGXVS69DNrYNOuW5FUjHGkxpeu7zYi5Vkqp3/ZMoGZeSZoIHWMi0mJK17cLtblSu8nDA4Yvb9ROg763bvsbEiMtpnT9kKX7WfAM0VD+euHgv3QHZgUyNKffwl/KODEXxcGsQPpCpbyiI2bhEJo3EWkxpesPhUp5RQevbSM0byLSYkrXNwmV5ooOzCwBTEKluKID71kC2IRyXdGhl+mmy0r5niJWgwlxCWW7osP8mcrU2h2KMX35Tn8CpMWUru++qsN1Rcf6XyHQ7OJi25f8MAuEIC2mdP1ZIS2mdP1ZIS2mdP1ZIS2mdP1ZIS2mdP1ZIS2mdP1Z0RdTuvGxQSRL3IukHOjuO0vc5eeDiTaAHwc7CMwqCJhVEDCrIGBWQcCsgoBZBQGzCgJmFQTMKgiYVRAwqyBgVkE0Rp1Q48cBAAAAAAAAAAAAAAAAAAAAAAAAAAAAAAAAAAAAAAC84MKEgsAlPwUBswoCZhUEzCoImFUQMKsgYFZBwKyCgFkFAbMKAmYVBMwqCJhVEDCrIGBWQcCsgoBZBQGzCgJmFQTMKgiYVRAwqyBgVkHArIKAWQUBswoCZhUEzCoImJWZTDeStjXcYDqGRqx/G0TM1mh8/jcBC41YL3IBczYan/9NwMIPqupzjWj/64S73zz+As+xoQXnx11MGQ9Um7Mr5pk+xqyxY4GOsc/2WLPGjgMYY57xsWaNGQMYGPOsjzFrTH3gIPaZH2NWbG3gIfbZH2pWbF0QSMwMCDUrpmY6lDpZtVAot64fWJuplqmPUnean3vV5csP8fTUxMyCELNi6qVFixcKF503k1k8ZzP/jSqDaaEzIcSs0Frp0aKFEptP8D5kDBnUGqVNu9HrkZzQ2eAzK7SODFxIH7H5hK2PNm0dv8BTUhIyI3xmhdSQwyakjdh8wtenru92OU/wUEpCZoXLrJD+sviE5MTmE74+Sj23itNPYXwzw2WWr688PiE5sfmErw/NqDbnLg+lxjc7bGb5+uXBJyRH5/NmWgVq/GNcCMhJhmuG2Mxy9clHrEjcpALNcs0Sk1mu/LzEihSbT/j6ZHwZ1NhmisksW25+fEJyYvMJX5+6fr7L+SkPSWGbLdwsW9528AnJic0nfH0yLd05phnDzTLlbA+fkJzYfMLXZx0X/VDMMc2avlmmOK+RF5+QnNh8wtZnuIORHT5z+mbxGO+bn1ihYvMJ3mcLe4M2+OzR5vDj259VhBbL1viSnMd54/m+Ppl23V30Z5Bplu3GrCJM55pc4sfm2/pkPJ/loz+Lem3HZhU4xzS7dmtWgXNMswuzKgPXcBVJOVzDVSTlgJk1E7To/DjYQWBWQcCsgggxa9neve72cVVd5DGQkUCzXqGcZiFxBsO2SIhZP6yqR5uc1zrD7jQ/L/EckIEQswgYtgOEmkXkMWy4C363+6IlnVZ3n609OrrY5N0c7KLTMYqZGI5nb6Zd+4zEmEXIG8YF2my3J4p+a3DaI6yfbn/Y6JuZWLMIWcO0MC30nb0nupn15y52ZjRsLfrmLBrOtr1erzDoSdL2XfBQTsaYRcgZtmnWmlb0s3NDYll/n+J1HnJycPBk1++tan//YR7OyVizCBnDbGYRrWH2uItnn/3wqL5Kvdz1+x4P5WaKWQR97qLPX51hzs9hy6Bbw/sE9cVtjJlZh4df6fr8q5lVj/BwbqaaRYTOsLCxfGb44iZoRir1Ztc3/D1LqRdXfZT6MQ9tgzAB/YQYFjaWzwxfnLP5Xnc6WA3aWCw+1eT/tzHqneZ965M8vA3CBAzDZ1jYWD4zfPE+Tz/9aCP2a93suNO8lH2Cp1ip6591Y13noW0RJmA4LsPCxvKZ4YtrphhFuXX99mpmXbnyGR7eFmECxmEzLGwsnxm+ODHFKEKpn3Tj/JyHtkmIgMsRp0hMhoWM5Taj/WqzPU5MNeqppz7W9Pvnqv/BwZd5eJuECLgceYqEcvvL+pCx3Gb5lt9TjSKU+n7X/yUe2jYhAppmCc+x0e8bMpbdLN/yO4VR9MFZqXurGoeH3+DhbRMmoN+wZftSeW6Iq/X7Ddk0y7Q3OFx+pzCKqOujrsbvKt8O/xYIE7DFZViEWYE7GOZm3nVX6hVDrrm5TnPQrnqb920e2gVizCJchqVheMrCfz5r2MfeXGa1dYanUXaEWLMIecOAkTFmETBsC4w1i4BhmZliFsE/S9FjnqNZBp0iAVammkWEzrAUY82aVAKGGJZqrNmSUkCfYSnHmiWpBXQZlnqs2SEhoM0wibFmhZSAJsOkxpoNkgLyZb3kWLNAWsD4UyTASioBl+G77pPHmi2pBIwwCzsYY0llFsgAzCoImFUQMCsz9KZteCPP1bBgiKH5wPmqQcQsjcbmfw9wYNra4Tmp4GMdV9W4b33NGS6ihGF8DBg1AS5mSsN4bRiVAC5qCsN4TRiVEC7uFMN4LRglABd5jGG8BowShIsdYxjvC6MywEUPMYz3gVEZ4eK7DOO5MGoLcBNMhvEcGLVFuBl9w3gMRu0A3BQyjB+DUTvEMfvWUf93ivF8sGX6hsGoAugMe5UajAIAAAAAAAAAAAAAAAAAAAAAAAAAALtPex+VvdVNAtb/tpx+37P+a3L61+VK/bo6Pv4QD61o4yf88Dn8X6j7xgOVvuHa6eB/zK/bLd5lxTpuvourjtsYjqNNe6OCaQbaGdUa1d5LpRWpP9Nss2Mt7r1qsfgoDwebRazHI6N03Rusx8zRdyYio0y35nCxOSOGd3ONMUujTTPFZk0rjL6/yfDORD76Zin1j+qZZz5ujNtwxXUML4Ud62fwH62LBBdro17qfm7e1dVlBuGK0z3I2nj8k+gDyVRBtNh1/aWm3a/a+1A+NojbcMV9N46bHVqssS81fbHp/pPt4+vGuAlXPOSWjLNiqhj9/nRXV6Xeq9p7J392EDcxNT4rtBimmdX/wOpbuq8fX++OtXd55XGOK46ZxXC9Z/HdBRM8tlhcavr9p6L3r8Xiq4M4xxXHexYjZDXoFnQYoxUhHdMrRB7v44q7nkizJORzllvQYWx//5Hm2N/PYzzexxXXMdNL9Gzx7WCECMqh3YyxZmEHw4Fvb9Almi22v/9wU+tP1rimH8feYCBTd91N0E68K04Mx9EmYdfdyfqZHXs+y7yspwULmWyLE3zF6RsPAAAAAAAAAAAAoFj+D9fVcMVEXRVaAAAAAElFTkSuQmCC"), .license("Unspecified"), .width(107)) image_1: pin names not known
  Button button_1 (.out(button_1_out));
  Synchroniser synchroniser_1 (
    .\input (button_1_out), .Counter(synchroniser_1_counter), .CLK(synchroniser_1_clk),
    .DONE(synchroniser_1_done));
  register_8bit register_8bit_1 (.D(out_3), .CLK(synchroniser_1_clk), .Q(register_8bit_1_q));  // open: Qcomplement
  Control_unit control_unit_1 (
    .Counter(synchroniser_1_counter), .SUB_A(Sign[8]), .SUB_B(Sign_2[8]), .F(register_8bit_1_q),
    .A(Sign[7:0]), .B(Sign_2[7:0]), .OUTA(control_unit_1_outa), .OUTB(control_unit_1_outb),
    .Negate(control_unit_1_negate));
  not not_1 (not_1_out, synchroniser_1_counter[1]);
  and and_1 (and_1_out, synchroniser_1_counter[0], not_1_out);
  and and_2 (and_2_out, and_1_out, Sign[8]);
  and and_3 (and_3_out, and_1_out, Sign_2[8]);
  adder_8bit adder_8bit_1 (
    .SUB_B(and_3_out), .SUB_A(and_2_out), .B(control_unit_1_outb), .A(control_unit_1_outa), .S(out_3));  // open: Cout
  OverflowDetection overflowdetection_1 (
    .SUB_A(Sign[8]), .SUB_B(Sign_2[8]), .NEGATE(control_unit_1_negate), .V(overflowdetection_1_v));
  not not_2 (not_2_out, synchroniser_1_done);
  not not_3 (not_3_out, synchroniser_1_done);
  and and_4 (and_4_out, synchroniser_1_done, out_4);
  and and_5 (and_5_out, control_unit_1_negate, not_2_out);
  and and_6 (and_6_out, synchroniser_1_done, out_5);
  and and_7 (and_7_out, overflowdetection_1_v, not_3_out);
  or or_1 (or_1_out, and_4_out, and_5_out);
  or or_2 (or_2_out, and_6_out, and_7_out);
  D_Flip_Flop d_ff_1 (.D(or_1_out), .clk(synchroniser_1_clk), .Q(out_4));  // open: Qn, preset, reset
  D_Flip_Flop d_ff_2 (.D(or_2_out), .clk(synchroniser_1_clk), .Q(out_5));  // open: Qn, preset, reset

  // Notes on the sheet:
  //   REG F
  //   A
  //   B
endmodule

module Half_adder (
  input  A,
  input  B,
  output S,
  output Cout
);

  xor xor_1 (S, A, B);
  and and_1 (Cout, B, A);
endmodule

module Full_adder (
  input  A,
  input  B,
  input  Cin,
  output S,
  output Cout
);

  wire half_adder_1_cout, half_adder_1_s, half_adder_2_cout;

  Half_adder half_adder_1 (.A(A), .B(B), .S(half_adder_1_s), .Cout(half_adder_1_cout));
  Half_adder half_adder_2 (.A(half_adder_1_s), .B(Cin), .S(S), .Cout(half_adder_2_cout));
  or or_1 (Cout, half_adder_2_cout, half_adder_1_cout);
endmodule

module adder_8bit (
  input  [7:0] A,
  input  [7:0] B,
  input  SUB_A,
  input  SUB_B,
  output Cout,
  output [7:0] S
);

  wire full_adder_1_cout, full_adder_2_cout, full_adder_3_cout, full_adder_4_cout, full_adder_5_cout,
       full_adder_6_cout, full_adder_7_cout, xor_1_out;
  wire [7:0] one_complement_8bit_1_c, one_complement_8bit_2_c;

  one_complement_8bit one_complement_8bit_1 (.A(A), .E(SUB_A), .C(one_complement_8bit_1_c));
  one_complement_8bit one_complement_8bit_2 (.A(B), .E(SUB_B), .C(one_complement_8bit_2_c));
  xor xor_1 (xor_1_out, SUB_A, SUB_B);
  Full_adder full_adder_1 (
    .A(one_complement_8bit_1_c[0]), .B(one_complement_8bit_2_c[0]), .Cin(xor_1_out), .S(S[0]),
    .Cout(full_adder_1_cout));
  Full_adder full_adder_2 (
    .A(one_complement_8bit_1_c[1]), .B(one_complement_8bit_2_c[1]), .Cin(full_adder_1_cout), .S(S[1]),
    .Cout(full_adder_2_cout));
  Full_adder full_adder_3 (
    .A(one_complement_8bit_1_c[2]), .B(one_complement_8bit_2_c[2]), .Cin(full_adder_2_cout), .S(S[2]),
    .Cout(full_adder_3_cout));
  Full_adder full_adder_4 (
    .A(one_complement_8bit_1_c[3]), .B(one_complement_8bit_2_c[3]), .Cin(full_adder_3_cout), .S(S[3]),
    .Cout(full_adder_4_cout));
  Full_adder full_adder_5 (
    .A(one_complement_8bit_1_c[4]), .B(one_complement_8bit_2_c[4]), .Cin(full_adder_4_cout), .S(S[4]),
    .Cout(full_adder_5_cout));
  Full_adder full_adder_6 (
    .A(one_complement_8bit_1_c[5]), .B(one_complement_8bit_2_c[5]), .Cin(full_adder_5_cout), .S(S[5]),
    .Cout(full_adder_6_cout));
  Full_adder full_adder_7 (
    .A(one_complement_8bit_1_c[6]), .B(one_complement_8bit_2_c[6]), .Cin(full_adder_6_cout), .S(S[6]),
    .Cout(full_adder_7_cout));
  Full_adder full_adder_8 (
    .A(one_complement_8bit_1_c[7]), .B(one_complement_8bit_2_c[7]), .Cin(full_adder_7_cout), .S(S[7]),
    .Cout(Cout));
endmodule

module two_complement_8bit (
  input  [7:0] A,
  input  E,
  output [7:0] C
);

  wire [7:0] xor_1_out;

  xor xor_1 (xor_1_out[0], A[0], E);
  xor xor_2 (xor_1_out[1], A[1], E);
  xor xor_3 (xor_1_out[2], A[2], E);
  xor xor_4 (xor_1_out[3], A[3], E);
  xor xor_5 (xor_1_out[4], A[4], E);
  xor xor_6 (xor_1_out[5], A[5], E);
  xor xor_7 (xor_1_out[6], A[6], E);
  xor xor_8 (xor_1_out[7], A[7], E);
  adder_8bit adder_8bit_1 (.SUB_B(1'b0), .SUB_A(1'b0), .B({{7{1'b0}}, E}), .A(xor_1_out), .S(C));  // open: Cout
endmodule

module one_complement_8bit (
  input  [7:0] A,
  input  E,
  output [7:0] C
);

  xor xor_1 (C[0], A[0], E);
  xor xor_2 (C[1], A[1], E);
  xor xor_3 (C[2], A[2], E);
  xor xor_4 (C[3], A[3], E);
  xor xor_5 (C[4], A[4], E);
  xor xor_6 (C[5], A[5], E);
  xor xor_7 (C[6], A[6], E);
  xor xor_8 (C[7], A[7], E);
endmodule

module register_8bit (
  input  [7:0] D,
  input  CLK,
  output [7:0] Q,
  output [7:0] Qcomplement
);

  D_Flip_Flop d_ff_1 (.D(D[0]), .clk(CLK), .Q(Q[0]), .Qn(Qcomplement[0]));  // open: preset, reset
  D_Flip_Flop d_ff_2 (.D(D[1]), .clk(CLK), .Q(Q[1]), .Qn(Qcomplement[1]));  // open: preset, reset
  D_Flip_Flop d_ff_3 (.D(D[2]), .clk(CLK), .Q(Q[2]), .Qn(Qcomplement[2]));  // open: preset, reset
  D_Flip_Flop d_ff_4 (.D(D[3]), .clk(CLK), .Q(Q[3]), .Qn(Qcomplement[3]));  // open: preset, reset
  D_Flip_Flop d_ff_5 (.D(D[4]), .clk(CLK), .Q(Q[4]), .Qn(Qcomplement[4]));  // open: preset, reset
  D_Flip_Flop d_ff_6 (.D(D[5]), .clk(CLK), .Q(Q[5]), .Qn(Qcomplement[5]));  // open: preset, reset
  D_Flip_Flop d_ff_7 (.D(D[6]), .clk(CLK), .Q(Q[6]), .Qn(Qcomplement[6]));  // open: preset, reset
  D_Flip_Flop d_ff_8 (.D(D[7]), .clk(CLK), .Q(Q[7]), .Qn(Qcomplement[7]));  // open: preset, reset
endmodule

module clock_counter (
  input  CLK,
  input  D,
  output [1:0] out_3,
  output Done
);

  wire and_1_out, and_2_out, not_1_out, not_2_out, not_3_out, xor_1_out;

  xor xor_1 (xor_1_out, out_3[1], out_3[0]);
  not not_1 (not_1_out, out_3[0]);
  and and_1 (and_1_out, D, xor_1_out);
  and and_2 (and_2_out, D, not_1_out);
  D_Flip_Flop d_ff_1 (.D(and_1_out), .clk(CLK), .Q(out_3[1]));  // open: Qn, preset, reset
  D_Flip_Flop d_ff_2 (.D(and_2_out), .clk(CLK), .Q(out_3[0]));  // open: Qn, preset, reset
  not not_2 (not_2_out, out_3[1]);
  not not_3 (not_3_out, out_3[0]);
  and and_3 (Done, not_2_out, not_3_out);
endmodule

module Synchroniser (
  input  \input ,
  output [1:0] Counter,
  output DONE,
  output CLK
);

  wire and_1_out, not_1_out, or_1_out;

  not not_1 (not_1_out, DONE);
  Clock clock_1 (.out(CLK));
  and and_1 (and_1_out, \input , DONE);
  or or_1 (or_1_out, and_1_out, not_1_out);
  clock_counter clock_counter_1 (.CLK(CLK), .D(or_1_out), .out_3(Counter), .Done(DONE));
endmodule

module Control_unit (
  input  [7:0] A,
  input  [7:0] B,
  input  SUB_A,
  input  SUB_B,
  input  [7:0] F,
  input  [1:0] Counter,
  output [7:0] OUTA,
  output [7:0] OUTB,
  output Negate
);

  wire [1:1] and_1_out;
  wire [7:0] one_complement_8bit_1_c;

  and and_1 (and_1_out[1], SUB_A, SUB_B);
  one_complement_8bit one_complement_8bit_1 (.A(F), .E(F[7]), .C(one_complement_8bit_1_c));
  Multiplexer #(.select(2), .width(8)) multiplexer_1 (
    .in0(one_complement_8bit_1_c), .in1(A), .in2(F), .in3(one_complement_8bit_1_c), .out(OUTA), .sel(Counter));
  Multiplexer #(.select(2), .width(8)) multiplexer_2 (
    .in0({8{1'b0}}), .in1(B), .in2({{6{1'b0}}, and_1_out[1], 1'b0}), .in3({{7{1'b0}}, F[7]}), .out(OUTB),
    .sel(Counter));

  assign Negate = F[7];
endmodule

module OverflowDetection (
  input  SUB_A,
  input  SUB_B,
  input  NEGATE,
  output V
);

  wire not_1_out, xor_1_out, xor_2_out;

  xor xor_1 (xor_1_out, SUB_A, SUB_B);
  xor xor_2 (xor_2_out, SUB_A, NEGATE);
  not not_1 (not_1_out, xor_1_out);
  and and_1 (V, not_1_out, xor_2_out);
endmodule
